# Fritzing sketch Count Up Box Schematic (saved by Fritzing 0.8.7b)
circuit board: 2.96295cm x 3.44867cm
circuit board: 10cm x 10cm
breadboards: 3

parts:
  Batt_+ = female pin header, 1 pin [form="♀ (female)"]
  Batt_- = female pin header, 1 pin [form="♀ (female)"]
  R14 = Resistor [tolerance=±5% resistance=10k package=THT]
  R15 = Resistor [tolerance=±5% resistance=10k package=THT]
  Xtal = female pin header, 1 pin [form="♀ (female)"]
  32_kHz = female pin header, 1 pin [form="♀ (female)"]
  Part1 = Arduino Nano (Rev3.0)
  ENCODER2 = Rotary Encoder with Knob
  R16 = Resistor [tolerance=±5% resistance=10k package=THT]
  R17 = Resistor [tolerance=±5% resistance=10k package=THT]
  R18 = Resistor [tolerance=±5% resistance=220 package=THT]
  IC4 = DS1307 [package=THT]
  LCD_Pins = female pin header, 4 pins [form="♀ (female)"]
  J8 = female pin header, 5 pins [form="♀ (female)"]
  Rotary_Encoder = female pin header, 5 pins [form="♀ (female)"]
  VCC1 = Battery

nets:
  N1: Batt_+.pin1, IC4.Vbat_-_Backup_Supply
  N2: Batt_-.pin1, Part1.GND, ENCODER2.no_name_yet#2, R18.Pin_1, IC4.0V, LCD_Pins.pin4, J8.pin4, Rotary_Encoder.pin4, VCC1.-
  N3: R14.Pin_0, R15.Pin_0, Part1.5V, ENCODER2.no_name_yet#4, R16.Pin_0, R17.Pin_0, IC4.+V, LCD_Pins.pin3, J8.pin2, Rotary_Encoder.pin2, VCC1.+
  N4: R14.Pin_1, Part1.A5, IC4.SCL_-_I2C_Clock, LCD_Pins.pin1
  N5: R15.Pin_1, Part1.A4, IC4.SDA_-_I2C_Data, LCD_Pins.pin2
  N6: Xtal.pin1, IC4.X2_-_Crystal
  N7: 32_kHz.pin1, IC4.X1_-_Crystal
  N8: Part1.D6, ENCODER2.no_name_yet#1, R16.Pin_1, J8.pin5, Rotary_Encoder.pin5
  GND: Part1.D7, ENCODER2.no_name_yet#3, R17.Pin_1, J8.pin3, Rotary_Encoder.pin3
  N9: Part1.D8, ENCODER2.no_name_yet#5, R18.Pin_0, J8.pin1, Rotary_Encoder.pin1

custom parts:
  Rotary Encoder with Knob: Rotary Encoder with 1/4" Shaft and Knob
