# Fritzing sketch Count Up Box Schematic Production (saved by Fritzing 0.8.5b)
circuit board: 5.25138cm x 7.46399cm
breadboards: 3

parts:
  Batt_+ = female pin header, 1 pin [form="♀ (female)"]
  Batt_- = female pin header, 1 pin [form="♀ (female)"]
  10K = Resistor [tolerance=±5% resistance=10k package=THT]
  Xtal = female pin header, 1 pin [form="♀ (female)"]
  32_kHz = female pin header, 1 pin [form="♀ (female)"]
  Nano = Arduino Nano (Rev3.0)
  IC4 = DS1307 [package=THT]
  LCD_Pins = female pin header, 4 pins [form="♀ (female)"]
  Rotary_Encoder = female pin header, 5 pins [form="♀ (female)"]
  10K_2 = Resistor [tolerance=±5% resistance=10k package=THT]

nets:
  N1: Batt_+.pin1, IC4.Vbat_-_Backup_Supply
  N2: Batt_-.pin1, Nano.GND, IC4.0V, LCD_Pins.pin4, Rotary_Encoder.pin4
  N3: 10K.Pin_0, Nano.5V, IC4.+V, LCD_Pins.pin3, Rotary_Encoder.pin2, 10K_2.Pin_0
  N4: 10K.Pin_1, Nano.A5, IC4.SCL_-_I2C_Clock, LCD_Pins.pin2
  N5: Xtal.pin1, IC4.X2_-_Crystal
  N6: 32_kHz.pin1, IC4.X1_-_Crystal
  N7: Nano.D6, Rotary_Encoder.pin5
  N8: Nano.D7, Rotary_Encoder.pin3
  N9: Nano.D8, Rotary_Encoder.pin1
  N10: Nano.A4, IC4.SDA_-_I2C_Data, LCD_Pins.pin1, 10K_2.Pin_1

notes:
  J <3 Z
