# Fritzing sketch Count Up Box Schematic (saved by Fritzing 0.8.5b)
circuit board: 3.21113cm x 3.63481cm
circuit board: 10cm x 10cm
breadboards: 3

parts:
  Batt_+ = female pin header, 1 pin [form="♀ (female)"]
  Batt_- = female pin header, 1 pin [form="♀ (female)"]
  R14 = Resistor [tolerance=±5% resistance=10k package=THT]
  R15 = Resistor [tolerance=±5% resistance=10k package=THT]
  Xtal = female pin header, 1 pin [form="♀ (female)"]
  32_kHz = female pin header, 1 pin [form="♀ (female)"]
  Part1 = Arduino Nano (Rev3.0)
  ENCODER2 = Rotary Encoder with Knob
  R16 = Resistor [tolerance=±5% resistance=10k package=THT]
  R17 = Resistor [tolerance=±5% resistance=10k package=THT]
  R18 = Resistor [tolerance=±5% resistance=220 package=THT]
  J4 = female pin header, 1 pin [form="♀ (female)"]
  J5 = female pin header, 1 pin [form="♀ (female)"]
  J6 = female pin header, 1 pin [form="♀ (female)"]
  IC4 = DS1307 [package=THT]
  LCD_Pins = female pin header, 4 pins [form="♀ (female)"]
  J8 = female pin header, 5 pins [form="♀ (female)"]
  J9 = female pin header, 5 pins [form="♀ (female)"]

nets:
  N1: Batt_+.pin1, IC4.Vbat_-_Backup_Supply
  N2: Batt_-.pin1, Part1.GND, ENCODER2.no_name_yet#2, R18.Pin_1, IC4.0V, LCD_Pins.pin4
  N3: R14.Pin_0, R15.Pin_0, Part1.5V, ENCODER2.no_name_yet#4, R16.Pin_0, R17.Pin_0, IC4.+V, LCD_Pins.pin3
  N4: R14.Pin_1, Part1.A5, IC4.SCL_-_I2C_Clock, LCD_Pins.pin1
  N5: R15.Pin_1, Part1.A4, IC4.SDA_-_I2C_Data, LCD_Pins.pin2
  N6: Xtal.pin1, IC4.X2_-_Crystal
  N7: 32_kHz.pin1, IC4.X1_-_Crystal
  N8: Part1.D6, ENCODER2.no_name_yet#5, R18.Pin_0, J4.pin1
  N9: Part1.D7, ENCODER2.no_name_yet#3, R17.Pin_1, J6.pin1
  N10: Part1.D8, ENCODER2.no_name_yet#1, R16.Pin_1, J5.pin1
  N11: J8.pin1, J9.pin1
  N12: J8.pin2, J9.pin2
  N13: J8.pin3, J9.pin3
  N14: J8.pin4, J9.pin4
  N15: J8.pin5, J9.pin5

notes:
  *

custom parts:
  Rotary Encoder with Knob: Rotary Encoder with 1/4" Shaft and Knob
