# Fritzing sketch Rotary Encoder Mini Board (saved by Fritzing 0.8.7b)
circuit board: 2.96295cm x 3.44867cm
breadboards: 1

parts:
  ENCODER2 = Rotary Encoder with Knob
  R16 = Resistor [tolerance=±5% resistance=10k package=THT]
  R17 = Resistor [tolerance=±5% resistance=10k package=THT]
  R18 = Resistor [tolerance=±5% resistance=220 package=THT]
  J8 = female pin header, 5 pins [form="♀ (female)"]

nets:
  N1: ENCODER2.no_name_yet#1, R16.Pin_1, J8.pin5
  N2: ENCODER2.no_name_yet#2, R18.Pin_1, J8.pin4
  GND: ENCODER2.no_name_yet#3, R17.Pin_1, J8.pin3
  N3: ENCODER2.no_name_yet#4, R16.Pin_0, R17.Pin_0, J8.pin2
  N4: ENCODER2.no_name_yet#5, R18.Pin_0, J8.pin1

custom parts:
  Rotary Encoder with Knob: Rotary Encoder with 1/4" Shaft and Knob
